// Logisim project alu.circ as structural Verilog: 6 circuits, main circuit main
module main (
  input  [31:0] X,
  input  [31:0] Y,
  input  [5:0] Switch__S,
  output Signed_Overflow,
  output [31:0] RESULT,
  output Equal
);

  wire ADD_Carry, bitpal_1_out, comparator_1_lt, comparator_2_lt, SUB_Carry;
  wire [4:0] bit_extender_1_out, bit_extender_2_out, bit_extender_3_out, Switch_5;
  wire [31:0] ADD, AND, BITPAL, LFSR, LUI, OR, SLL, SLT, SLTU, SRA, SRL, SUB;

  _6_to_5_switch u_6_to_5_switch_1 (.in_1(Switch__S), .out(Switch_5));
  assign AND = X & Y;  // AND_Gate and_1, 32 bits wide
  assign OR = X | Y;  // OR_Gate or_1, 32 bits wide
  bitpal bitpal_1 (.X(X), .out(bitpal_1_out));
  LFSR lfsr_1 (.in_1(X), .out(LFSR));
  Bit_Extender #(.in_width(32), .out_width(5)) bit_extender_1 (.in(Y), .out(bit_extender_1_out));
  Bit_Extender #(.in_width(32), .out_width(5)) bit_extender_2 (.in(Y), .out(bit_extender_2_out));
  Bit_Extender #(.in_width(32), .out_width(5)) bit_extender_3 (.in(Y), .out(bit_extender_3_out));
  Adder adder_1 (.X(X), .Y(Y), .out_2(ADD_Carry), .out(ADD));
  Subber subber_1 (.X(X), .Y(Y), .out_2(SUB_Carry), .out(SUB));
  Shifter #(.width(32)) shifter_1 (.in(Y), .\dist (5'b10000), .out(LUI));
  Comparator #(.width(32)) comparator_1 (.a(X), .b(Y), .lt(comparator_1_lt));  // open: gt, eq
  assign SLT = {{31{1'b0}}, comparator_1_lt};  // Bit_Extender bit_extender_4
  Comparator #(.width(32), .mode("unsigned")) comparator_2 (.a(X), .b(Y), .lt(comparator_2_lt));  // open: gt, eq
  assign SLTU = {{31{1'b0}}, comparator_2_lt};  // Bit_Extender bit_extender_5
  assign BITPAL = {{31{1'b0}}, bitpal_1_out};  // Bit_Extender bit_extender_6
  Comparator #(.width(32)) comparator_3 (.a(X), .b(Y), .eq(Equal));  // open: gt, lt
  Shifter #(.width(32)) shifter_2 (.in(X), .\dist (bit_extender_1_out), .out(SLL));
  Shifter #(.width(32), .shift("lr")) shifter_3 (.in(X), .\dist (bit_extender_2_out), .out(SRL));
  Shifter #(.width(32), .shift("ar")) shifter_4 (.in(X), .\dist (bit_extender_3_out), .out(SRA));
  Multiplexer #(.select(5), .width(32), .disabled(0), .enable("false")) multiplexer_1 (
    .in0(ADD), .in1(ADD), .in2(SUB), .in3(SUB), .in4(AND), .in5(OR), .in6(LUI), .in7({32{1'b0}}),
    .in8({32{1'b0}}), .in9({32{1'b0}}), .in10(SLT), .in11(SLTU), .in12({32{1'b0}}), .in13({32{1'b0}}),
    .in14({32{1'b0}}), .in15({32{1'b0}}), .in16(SLL), .in18(SRL), .in19(SRA), .in20({32{1'b0}}),
    .in21({32{1'b0}}), .in22({32{1'b0}}), .in23({32{1'b0}}), .in24({32{1'b0}}), .in25({32{1'b0}}),
    .in26({32{1'b0}}), .in27({32{1'b0}}), .in28({32{1'b0}}), .in29({32{1'b0}}), .in30(BITPAL), .in31(LFSR),
    .out(RESULT), .sel(Switch_5));  // open: in17
  Multiplexer #(.select(5), .disabled(0), .enable("false")) multiplexer_2 (
    .in0(ADD_Carry), .in1(1'b0), .in2(SUB_Carry), .in3(1'b0), .in4(1'b0), .in5(1'b0), .in6(1'b0), .in7(1'b0),
    .in8(1'b0), .in9(1'b0), .in10(1'b0), .in11(1'b0), .in12(1'b0), .in13(1'b0), .in14(1'b0), .in15(1'b0),
    .in16(1'b0), .in17(1'b0), .in18(1'b0), .in19(1'b0), .in20(1'b0), .in21(1'b0), .in22(1'b0), .in23(1'b0),
    .in24(1'b0), .in25(1'b0), .in26(1'b0), .in27(1'b0), .in28(1'b0), .in29(1'b0), .in30(1'b0), .in31(1'b0),
    .out(Signed_Overflow), .sel(Switch_5));

  // Other names for the same wires on the sheet: Carry = Signed_Overflow; Switch_6[5:0] = Switch__S

  // Notes on the sheet:
  //   INPUTS to your circuit
  //   INPUT to your circuit
  //   DON'T CHANGE THE INPUTS AND OUTPUTS! IF YOU DO SO, YOU NEED TO MAKE SURE THE PINS ARE IN THE RIGHT PLACES!
  //   OUTPUTS of your circuit
endmodule

module _6_to_5_switch (
  input  [5:0] in_1,
  output [4:0] out
);

  wire not_1_out, or_1_out;

  not not_1 (not_1_out, or_1_out);
  or or_1 (or_1_out, in_1[5], in_1[4]);
  or or_2 (out[4], not_1_out, in_1[4]);

  assign out[3:0] = in_1[3:0];
endmodule

module bitpal (
  input  [31:0] X,
  output out
);

  wire xnor_1_out, xnor_2_out, xnor_3_out, xnor_4_out, xnor_5_out, xnor_6_out, xnor_7_out, xnor_8_out,
       xnor_9_out, xnor_10_out, xnor_11_out, xnor_12_out, xnor_13_out, xnor_14_out, xnor_15_out, xnor_16_out;

  xnor xnor_1 (xnor_1_out, X[0], X[31]);
  xnor xnor_2 (xnor_2_out, X[1], X[30]);
  xnor xnor_3 (xnor_3_out, X[2], X[29]);
  xnor xnor_4 (xnor_4_out, X[3], X[28]);
  xnor xnor_5 (xnor_5_out, X[4], X[27]);
  xnor xnor_6 (xnor_6_out, X[5], X[26]);
  xnor xnor_7 (xnor_7_out, X[6], X[25]);
  xnor xnor_8 (xnor_8_out, X[7], X[24]);
  xnor xnor_9 (xnor_9_out, X[8], X[23]);
  xnor xnor_10 (xnor_10_out, X[9], X[22]);
  xnor xnor_11 (xnor_11_out, X[10], X[21]);
  xnor xnor_12 (xnor_12_out, X[11], X[20]);
  xnor xnor_13 (xnor_13_out, X[12], X[19]);
  xnor xnor_14 (xnor_14_out, X[13], X[18]);
  xnor xnor_15 (xnor_15_out, X[14], X[17]);
  xnor xnor_16 (xnor_16_out, X[15], X[16]);
  and and_1 (out, xnor_1_out, xnor_2_out, xnor_3_out, xnor_4_out, xnor_5_out, xnor_6_out, xnor_7_out, xnor_8_out, xnor_9_out, xnor_10_out, xnor_11_out, xnor_12_out, xnor_13_out, xnor_14_out, xnor_15_out, xnor_16_out);
endmodule

module LFSR (
  input  [31:0] in_1,
  output [31:0] out
);

  wire xor_1_out, xor_2_out;

  xor xor_1 (xor_1_out, in_1[30], in_1[31]);
  xor xor_2 (xor_2_out, in_1[28], xor_1_out);
  xor xor_3 (out[0], in_1[0], xor_2_out);

  assign out[31:1] = in_1[30:0];
endmodule

module Adder (
  input  [31:0] X,
  input  [31:0] Y,
  output [31:0] out,
  output out_2
);

  wire adder_1_cout, adder_2_cout;

  Adder_part #(.width(31)) adder_1 (.a(X[30:0]), .b(Y[30:0]), .out(out[30:0]), .cout(adder_1_cout));  // open: cin
  Adder_part #(.width(1)) adder_2 (.a(X[31]), .b(Y[31]), .out(out[31]), .cin(adder_1_cout), .cout(adder_2_cout));
  xor xor_1 (out_2, adder_1_cout, adder_2_cout);
endmodule

module Subber (
  input  [31:0] X,
  input  [31:0] Y,
  output [31:0] out,
  output out_2
);

  wire subtractor_1_bout, subtractor_2_bout;

  Subtractor #(.width(31)) subtractor_1 (
    .a(X[30:0]), .b(Y[30:0]), .out(out[30:0]), .bout(subtractor_1_bout));  // open: bin
  Subtractor #(.width(1)) subtractor_2 (
    .a(X[31]), .b(Y[31]), .out(out[31]), .bin(subtractor_1_bout), .bout(subtractor_2_bout));
  xor xor_1 (out_2, subtractor_1_bout, subtractor_2_bout);
endmodule
