// Logisim project cpu.circ as structural Verilog: 10 circuits, main circuit main
module main (
  input  [31:0] RS_READ_VALUE,
  input  [31:0] RT_READ_VALUE,
  input  [31:0] INSTRUCTION,
  input  CLOCK,
  input  RESET,
  output [31:0] t0,
  output [31:0] t1,
  output [31:0] t2,
  output [31:0] t3,
  output [4:0] RS,
  output [4:0] RT,
  output [4:0] Write_Register,
  output [31:0] RD_WRITE_VALUE,
  output RD_WRITE_ENABLE,
  output [23:0] FETCH_ADDRESS
);

  wire AccessByte, ALUSrc, and_1_out, Branch, BranchEq, Equal, Imm_ZeroExt, Jump, JumpAL, JumpReg,
       Load_ZeroExt, MemRead, MemtoReg, MemWrite, multiplexer_4_out, NOP, Overflow, RD_T_t, RegDst, RS_T_t,
       RT_T_t;
  wire [1:0] multiplexer_3_out, RD_T, RS_T, RT_T;
  wire [4:0] multiplexer_1_out, RD, SHAMT;
  wire [5:0] ALUOp, FUNCT, OPCODE;
  wire [15:0] IMM;
  wire [25:0] ADDRESS;
  wire [31:0] ALU_Result, imm_zeroext_1_imm32b, Jal_RA_Address, Mem_Data, MEM_data_mem_out,
       multiplexer_7_out, multiplexer_8_out, RS_Reg, RS_Use, RT_Reg, RT_Use;

  Multiplexer #(.width(5), .disabled(0), .enable("false")) multiplexer_1 (
    .in0(RT), .in1(RD), .out(multiplexer_1_out), .sel(RegDst));
  Multiplexer #(.width(5), .disabled(0), .enable("false")) multiplexer_2 (
    .in0(multiplexer_1_out), .in1({5{1'b1}}), .out(Write_Register), .sel(JumpAL));
  Instruction_Parse instruction_parse_1 (
    .INSTRUCTION(INSTRUCTION), .CLK(CLOCK), .NOP(NOP), .Immediate(IMM), .Address(ADDRESS), .Funct(FUNCT),
    .Shamt(SHAMT), .Rd(RD), .Rt(RT), .Rs(RS), .Opcode(OPCODE));
  T_Register_Select t_register_select_1 (
    .RS(RS), .RT(RT), .RD(RD), .RS_T(RS_T_t), .RS_2(RS_T), .RT_T(RT_T_t), .RT_2(RT_T), .RD_T(RD_T_t),
    .RD_2(RD_T));
  Control control_1 (
    .Opcode(OPCODE), .Funct(FUNCT), .RegDst(RegDst), .Jump(Jump), .JumpAL(JumpAL), .JumpReg(JumpReg),
    .Branch(Branch), .BranchEq(BranchEq), .MemRead(MemRead), .MemtoReg(MemtoReg), .ALUOp(ALUOp),
    .MemWrite(MemWrite), .ALUSrc(ALUSrc), .RegWrite(RD_WRITE_ENABLE), .Load_ZeroExt(Load_ZeroExt),
    .Imm_ZeroExt(Imm_ZeroExt), .Access_Byte(AccessByte));
  Multiplexer #(.width(2), .disabled(0), .enable("false")) multiplexer_3 (
    .in0(RT_T), .in1(RD_T), .out(multiplexer_3_out), .sel(RegDst));
  Multiplexer #(.disabled(0), .enable("false")) multiplexer_4 (
    .in0(RT_T_t), .in1(RD_T_t), .out(multiplexer_4_out), .sel(RegDst));
  regfile_main RegFile (
    .Read_register_1(RS_T), .Read_register_2(RT_T), .write_register(multiplexer_3_out),
    .write_data(RD_WRITE_VALUE), .t0_Value(t0), .t1_Value(t1), .t2_Value(t2), .t3_Value(t3),
    .RegWrite(and_1_out), .clock(CLOCK), .Read_Data_1(RS_Reg), .Read_Data_2(RT_Reg));
  and and_1 (and_1_out, multiplexer_4_out, RD_WRITE_ENABLE);
  Multiplexer #(.width(32), .disabled(0), .enable("false")) multiplexer_5 (
    .in0(RS_READ_VALUE), .in1(RS_Reg), .out(RS_Use), .sel(RS_T_t));
  Multiplexer #(.width(32), .disabled(0), .enable("false")) multiplexer_6 (
    .in0(RT_READ_VALUE), .in1(RT_Reg), .out(RT_Use), .sel(RT_T_t));
  PC pc_1 (
    .RG_Address(RS_Use), .Inst_Address(ADDRESS), .Immediate(IMM), .Branch(Branch), .BranchEq(BranchEq),
    .Equal(Equal), .Jump(Jump), .JumpReg(JumpReg), .Clock(CLOCK), .Reset(RESET), .RA_Address(Jal_RA_Address),
    .PC_Address(FETCH_ADDRESS));
  Imm_ZeroExt imm_zeroext_1 (.Imm(IMM), .ZeroExt(Imm_ZeroExt), .Imm32b(imm_zeroext_1_imm32b));
  Multiplexer #(.width(32), .disabled(0), .enable("false")) multiplexer_7 (
    .in0(RT_Use), .in1(imm_zeroext_1_imm32b), .out(multiplexer_7_out), .sel(ALUSrc));
  alu_main ALU (
    .Switch__S(ALUOp), .X(RS_Use), .Equal(Equal), .RESULT(ALU_Result), .Signed_Overflow(Overflow),
    .Y(multiplexer_7_out));
  LED led_1 (.in(Overflow));
  Multiplexer #(.width(32), .disabled(0), .enable("false")) multiplexer_8 (
    .in0(ALU_Result), .in1(Mem_Data), .out(multiplexer_8_out), .sel(MemtoReg));
  NOP nop_1 (.JUMP(Jump), .Branch(Branch), .BranchEQ(BranchEq), .Equal(Equal), .NOP(NOP));
  Multiplexer #(.width(32), .disabled(0), .enable("false")) multiplexer_9 (
    .in0(multiplexer_8_out), .in1(Jal_RA_Address), .out(RD_WRITE_VALUE), .sel(JumpAL));
  mem_main MEM (
    .Data_Mem_Addr(ALU_Result), .Data_Mem_In(RT_Use), .ACCESS_BYTE(AccessByte), .MEM_WRITE(MemWrite),
    .CLOCK(CLOCK), .Data_Mem_Out(MEM_data_mem_out));
  Extend_Byte extend_byte_1 (
    .Mem_Data(MEM_data_mem_out), .Load_ZeroExt(AccessByte), .AccessByte(Load_ZeroExt), .MemData_Out(Mem_Data));

  // Other names for the same wires on the sheet: CLK = CLOCK; PC_Address[23:0] = FETCH_ADDRESS;
  //   RegWrite = RD_WRITE_ENABLE; RS_Run[31:0] = RS_READ_VALUE; RT_Run[31:0] = RT_READ_VALUE;
  //   WriteData[31:0] = RD_WRITE_VALUE

  // Notes on the sheet:
  //   These are outputs/inputs from run.circ
  //   These are outputs to run.circ
endmodule

module Instruction_Parse (
  input  [31:0] INSTRUCTION,
  input  CLK,
  input  NOP,
  output [15:0] Immediate,
  output [25:0] Address,
  output [5:0] Funct,
  output [4:0] Shamt,
  output [4:0] Rd,
  output [4:0] Rt,
  output [4:0] Rs,
  output [5:0] Opcode
);

  wire register_2_q;
  wire [31:0] register_1_q;

  Register #(.width(32)) register_1 (.D(INSTRUCTION), .Q(register_1_q), .clk(CLK));  // open: en, clr
  Register #(.width(1)) register_2 (.D(NOP), .Q(register_2_q), .clk(CLK));  // open: en, clr
  Multiplexer #(.width(32), .disabled(0), .enable("false")) multiplexer_1 (
    .in0(register_1_q), .in1({32{1'b0}}), .out({Opcode, Address}), .sel(register_2_q));

  assign Funct = Address[5:0];
  assign Immediate = Address[15:0];
  assign Rd = Address[15:11];
  assign Rs = Address[25:21];
  assign Rt = Address[20:16];
  assign Shamt = Address[10:6];

  // Other names for the same wires on the sheet: IMM[15:0] = Address[15:0]
endmodule

module Control (
  input  [5:0] Opcode,
  input  [5:0] Funct,
  output RegDst,
  output Jump,
  output JumpAL,
  output JumpReg,
  output Branch,
  output BranchEq,
  output MemRead,
  output MemtoReg,
  output [5:0] ALUOp,
  output MemWrite,
  output ALUSrc,
  output RegWrite,
  output Load_ZeroExt,
  output Imm_ZeroExt,
  output Access_Byte
);

  wire comparator_3_eq, comparator_4_eq, comparator_5_eq, comparator_6_eq, comparator_8_eq, comparator_10_eq,
       comparator_11_eq, comparator_12_eq, comparator_13_eq, or_3_out;

  Comparator #(.width(6)) comparator_1 (.a(Opcode), .b({6{1'b0}}), .eq(RegDst));  // open: gt, lt
  Jump jump_1 (.Opcode(Opcode), .Funct(Funct), .Jump(Jump), .JumpAL(JumpAL), .JumpReg(JumpReg));
  Comparator #(.width(6)) comparator_2 (.a(Opcode), .b(6'b000100), .eq(BranchEq));  // open: gt, lt
  Comparator #(.width(6)) comparator_3 (.a(Opcode), .b(6'b000101), .eq(comparator_3_eq));  // open: gt, lt
  Comparator #(.width(6)) comparator_4 (.a(Opcode), .b(6'b100000), .eq(comparator_4_eq));  // open: gt, lt
  Comparator #(.width(6)) comparator_5 (.a(Opcode), .b(6'b100011), .eq(comparator_5_eq));  // open: gt, lt
  Comparator #(.width(6)) comparator_6 (.a(Opcode), .b(6'b100100), .eq(comparator_6_eq));  // open: gt, lt
  ALUOp aluop_1 (.Opcode(Opcode), .Funct(Funct), .ALUOp(ALUOp));
  Comparator #(.width(6)) comparator_7 (.a(Opcode), .b(6'b101011), .eq(MemWrite));  // open: gt, lt
  Comparator #(.width(6)) comparator_8 (.a(Opcode), .b({6{1'b0}}), .eq(comparator_8_eq));  // open: gt, lt
  Comparator #(.width(6)) comparator_9 (.a(Opcode), .b(6'b100100), .eq(Load_ZeroExt));  // open: gt, lt
  Comparator #(.width(6)) comparator_10 (.a(Opcode), .b(6'b001100), .eq(comparator_10_eq));  // open: gt, lt
  Comparator #(.width(6)) comparator_11 (.a(Opcode), .b(6'b001101), .eq(comparator_11_eq));  // open: gt, lt
  Comparator #(.width(6)) comparator_12 (.a(Opcode), .b(6'b100000), .eq(comparator_12_eq));  // open: gt, lt
  Comparator #(.width(6)) comparator_13 (.a(Opcode), .b(6'b100100), .eq(comparator_13_eq));  // open: gt, lt
  or or_1 (Branch, BranchEq, comparator_3_eq);
  or or_2 (MemRead, comparator_4_eq, comparator_5_eq, comparator_6_eq);
  and and_1 (ALUSrc, ~comparator_8_eq, ~Branch);  // AND_Gate
  or or_3 (or_3_out, Jump, Branch, MemWrite);
  not not_1 (RegWrite, or_3_out);
  or or_4 (Imm_ZeroExt, comparator_10_eq, comparator_11_eq);
  or or_5 (Access_Byte, comparator_12_eq, comparator_13_eq);

  assign MemtoReg = MemRead;

  // Other names for the same wires on the sheet: FN[5:0] = Funct; OP[5:0] = Opcode
endmodule

module Jump (
  input  [5:0] Opcode,
  input  [5:0] Funct,
  output Jump,
  output JumpAL,
  output JumpReg
);

  wire comparator_1_eq, comparator_3_eq, comparator_4_eq;

  Comparator #(.width(6)) comparator_1 (.a(Opcode), .b(6'b000010), .eq(comparator_1_eq));  // open: gt, lt
  Comparator #(.width(6)) comparator_2 (.a(Opcode), .b(6'b000011), .eq(JumpAL));  // open: gt, lt
  Comparator #(.width(6)) comparator_3 (.a(Opcode), .b({6{1'b0}}), .eq(comparator_3_eq));  // open: gt, lt
  and and_1 (JumpReg, comparator_3_eq, comparator_4_eq);
  Comparator #(.width(6)) comparator_4 (.a(Funct), .b(6'b001000), .eq(comparator_4_eq));  // open: gt, lt
  or or_1 (Jump, comparator_1_eq, JumpAL, JumpReg);
endmodule

module ALUOp (
  input  [5:0] Opcode,
  input  [5:0] Funct,
  output [5:0] ALUOp
);

  wire comparator_1_eq, comparator_2_eq, comparator_3_eq, comparator_4_eq, comparator_5_eq, comparator_6_eq,
       comparator_7_eq, comparator_8_eq, comparator_9_eq, not_1_out, or_1_out;
  wire [5:0] and_1_out, and_2_out, and_3_out, and_4_out, and_5_out, and_6_out, and_7_out, bit_extender_1_out,
       bit_extender_2_out, bit_extender_3_out, bit_extender_4_out, bit_extender_5_out, bit_extender_6_out,
       or_2_out;

  Comparator #(.width(6)) comparator_1 (.a(Opcode), .b({6{1'b0}}), .eq(comparator_1_eq));  // open: gt, lt
  Comparator #(.width(6)) comparator_2 (.a(Opcode), .b(6'b001001), .eq(comparator_2_eq));  // open: gt, lt
  Comparator #(.width(6)) comparator_3 (.a(Opcode), .b(6'b001100), .eq(comparator_3_eq));  // open: gt, lt
  Comparator #(.width(6)) comparator_4 (.a(Opcode), .b(6'b001101), .eq(comparator_4_eq));  // open: gt, lt
  Comparator #(.width(6)) comparator_5 (.a(Opcode), .b(6'b001111), .eq(comparator_5_eq));  // open: gt, lt
  Comparator #(.width(6)) comparator_6 (.a(Opcode), .b(6'b100000), .eq(comparator_6_eq));  // open: gt, lt
  Comparator #(.width(6)) comparator_7 (.a(Opcode), .b(6'b100011), .eq(comparator_7_eq));  // open: gt, lt
  Comparator #(.width(6)) comparator_8 (.a(Opcode), .b(6'b100100), .eq(comparator_8_eq));  // open: gt, lt
  Comparator #(.width(6)) comparator_9 (.a(Opcode), .b(6'b101011), .eq(comparator_9_eq));  // open: gt, lt
  not not_1 (not_1_out, comparator_1_eq);
  or or_1 (or_1_out, comparator_6_eq, comparator_7_eq, comparator_8_eq, comparator_9_eq);
  assign bit_extender_1_out = {{5{not_1_out}}, not_1_out};  // Bit_Extender bit_extender_1
  assign bit_extender_2_out = {{5{comparator_2_eq}}, comparator_2_eq};  // Bit_Extender bit_extender_2
  assign bit_extender_3_out = {{5{comparator_3_eq}}, comparator_3_eq};  // Bit_Extender bit_extender_3
  assign bit_extender_4_out = {{5{comparator_4_eq}}, comparator_4_eq};  // Bit_Extender bit_extender_4
  assign bit_extender_5_out = {{5{comparator_5_eq}}, comparator_5_eq};  // Bit_Extender bit_extender_5
  assign bit_extender_6_out = {{5{or_1_out}}, or_1_out};  // Bit_Extender bit_extender_6
  assign and_1_out = bit_extender_2_out & 6'b100001;  // AND_Gate and_1, 6 bits wide
  assign and_2_out = bit_extender_3_out & 6'b100100;  // AND_Gate and_2, 6 bits wide
  assign and_3_out = bit_extender_4_out & 6'b100101;  // AND_Gate and_3, 6 bits wide
  assign and_4_out = bit_extender_5_out & 6'b100110;  // AND_Gate and_4, 6 bits wide
  assign and_5_out = bit_extender_6_out & 6'b100001;  // AND_Gate and_5, 6 bits wide
  assign or_2_out = and_1_out | and_2_out | and_3_out | and_4_out | and_5_out;  // OR_Gate or_2, 6 bits wide
  assign and_6_out = bit_extender_1_out & or_2_out;  // AND_Gate and_6, 6 bits wide
  assign ALUOp = and_6_out | and_7_out;  // OR_Gate or_3, 6 bits wide
  assign and_7_out = ~bit_extender_1_out & Funct;  // AND_Gate and_7, 6 bits wide

  // Other names for the same wires on the sheet: FN[5:0] = Funct
endmodule

module T_Register_Select (
  input  [4:0] RS,
  input  [4:0] RT,
  input  [4:0] RD,
  output RS_T,
  output [1:0] RS_2,
  output RT_T,
  output [1:0] RT_2,
  output RD_T,
  output [1:0] RD_2
);

  wire comparator_1_eq, comparator_2_eq, comparator_3_eq, comparator_4_eq, comparator_5_eq, comparator_6_eq,
       comparator_7_eq, comparator_8_eq, comparator_9_eq, comparator_10_eq, comparator_11_eq,
       comparator_12_eq;
  wire [1:0] and_1_out, and_2_out, and_3_out, and_4_out, and_5_out, and_6_out, and_7_out, and_8_out,
       and_9_out, and_10_out, and_11_out, and_12_out, bit_extender_1_out, bit_extender_2_out,
       bit_extender_3_out, bit_extender_4_out, bit_extender_5_out, bit_extender_6_out, bit_extender_7_out,
       bit_extender_8_out, bit_extender_9_out, bit_extender_10_out, bit_extender_11_out, bit_extender_12_out;

  Comparator #(.width(5)) comparator_1 (.a(RS), .b(5'b01000), .eq(comparator_1_eq));  // open: gt, lt
  Comparator #(.width(5)) comparator_2 (.a(RS), .b(5'b01001), .eq(comparator_2_eq));  // open: gt, lt
  Comparator #(.width(5)) comparator_3 (.a(RS), .b(5'b01010), .eq(comparator_3_eq));  // open: gt, lt
  Comparator #(.width(5)) comparator_4 (.a(RS), .b(5'b01011), .eq(comparator_4_eq));  // open: gt, lt
  Comparator #(.width(5)) comparator_5 (.a(RT), .b(5'b01000), .eq(comparator_5_eq));  // open: gt, lt
  Comparator #(.width(5)) comparator_6 (.a(RT), .b(5'b01001), .eq(comparator_6_eq));  // open: gt, lt
  Comparator #(.width(5)) comparator_7 (.a(RT), .b(5'b01010), .eq(comparator_7_eq));  // open: gt, lt
  Comparator #(.width(5)) comparator_8 (.a(RT), .b(5'b01011), .eq(comparator_8_eq));  // open: gt, lt
  Comparator #(.width(5)) comparator_9 (.a(RD), .b(5'b01000), .eq(comparator_9_eq));  // open: gt, lt
  Comparator #(.width(5)) comparator_10 (.a(RD), .b(5'b01001), .eq(comparator_10_eq));  // open: gt, lt
  Comparator #(.width(5)) comparator_11 (.a(RD), .b(5'b01010), .eq(comparator_11_eq));  // open: gt, lt
  Comparator #(.width(5)) comparator_12 (.a(RD), .b(5'b01011), .eq(comparator_12_eq));  // open: gt, lt
  or or_1 (RS_T, comparator_4_eq, comparator_3_eq, comparator_2_eq, comparator_1_eq);
  assign bit_extender_1_out = {{1{comparator_1_eq}}, comparator_1_eq};  // Bit_Extender bit_extender_1
  assign bit_extender_2_out = {{1{comparator_2_eq}}, comparator_2_eq};  // Bit_Extender bit_extender_2
  assign bit_extender_3_out = {{1{comparator_3_eq}}, comparator_3_eq};  // Bit_Extender bit_extender_3
  assign bit_extender_4_out = {{1{comparator_4_eq}}, comparator_4_eq};  // Bit_Extender bit_extender_4
  or or_2 (RT_T, comparator_8_eq, comparator_7_eq, comparator_6_eq, comparator_5_eq);
  assign bit_extender_5_out = {{1{comparator_5_eq}}, comparator_5_eq};  // Bit_Extender bit_extender_5
  assign bit_extender_6_out = {{1{comparator_6_eq}}, comparator_6_eq};  // Bit_Extender bit_extender_6
  assign bit_extender_7_out = {{1{comparator_7_eq}}, comparator_7_eq};  // Bit_Extender bit_extender_7
  assign bit_extender_8_out = {{1{comparator_8_eq}}, comparator_8_eq};  // Bit_Extender bit_extender_8
  or or_3 (RD_T, comparator_12_eq, comparator_11_eq, comparator_10_eq, comparator_9_eq);
  assign bit_extender_9_out = {{1{comparator_9_eq}}, comparator_9_eq};  // Bit_Extender bit_extender_9
  assign bit_extender_10_out = {{1{comparator_10_eq}}, comparator_10_eq};  // Bit_Extender bit_extender_10
  assign bit_extender_11_out = {{1{comparator_11_eq}}, comparator_11_eq};  // Bit_Extender bit_extender_11
  assign bit_extender_12_out = {{1{comparator_12_eq}}, comparator_12_eq};  // Bit_Extender bit_extender_12
  assign and_1_out = bit_extender_1_out & 2'b00;  // AND_Gate and_1, 2 bits wide
  assign and_2_out = bit_extender_2_out & 2'b01;  // AND_Gate and_2, 2 bits wide
  assign RS_2 = and_1_out | and_2_out | and_3_out | and_4_out;  // OR_Gate or_4, 2 bits wide
  assign and_3_out = bit_extender_3_out & 2'b10;  // AND_Gate and_3, 2 bits wide
  assign and_4_out = bit_extender_4_out & 2'b11;  // AND_Gate and_4, 2 bits wide
  assign and_5_out = bit_extender_5_out & 2'b00;  // AND_Gate and_5, 2 bits wide
  assign and_6_out = bit_extender_6_out & 2'b01;  // AND_Gate and_6, 2 bits wide
  assign RT_2 = and_5_out | and_6_out | and_7_out | and_8_out;  // OR_Gate or_5, 2 bits wide
  assign and_7_out = bit_extender_7_out & 2'b10;  // AND_Gate and_7, 2 bits wide
  assign and_8_out = bit_extender_8_out & 2'b11;  // AND_Gate and_8, 2 bits wide
  assign and_9_out = bit_extender_9_out & 2'b00;  // AND_Gate and_9, 2 bits wide
  assign and_10_out = bit_extender_10_out & 2'b01;  // AND_Gate and_10, 2 bits wide
  assign RD_2 = and_9_out | and_10_out | and_11_out | and_12_out;  // OR_Gate or_6, 2 bits wide
  assign and_11_out = bit_extender_11_out & 2'b10;  // AND_Gate and_11, 2 bits wide
  assign and_12_out = bit_extender_12_out & 2'b11;  // AND_Gate and_12, 2 bits wide
endmodule

module PC (
  input  [31:0] RG_Address,
  input  [25:0] Inst_Address,
  input  [15:0] Immediate,
  input  Branch,
  input  BranchEq,
  input  Equal,
  input  Jump,
  input  JumpReg,
  input  Clock,
  input  Reset,
  output [31:0] RA_Address,
  output [23:0] PC_Address
);

  wire BranchMux, xnor_1_out;
  wire [23:0] adder_2_out, bit_extender_1_out, bit_extender_2_out, bit_extender_3_out, multiplexer_1_out,
       multiplexer_2_out, multiplexer_3_out, RA_Address_t;

  Adder #(.width(24)) adder_1 (.a(24'h1), .b(PC_Address), .out(RA_Address_t));  // open: cin, cout
  assign bit_extender_1_out = {{8{Immediate[15]}}, Immediate};  // Bit_Extender bit_extender_1
  and and_1 (BranchMux, Branch, xnor_1_out);
  xnor xnor_1 (xnor_1_out, BranchEq, Equal);
  Adder #(.width(24)) adder_2 (.a(PC_Address), .b(bit_extender_1_out), .out(adder_2_out));  // open: cin, cout
  Multiplexer #(.width(24), .disabled(0), .enable("false")) multiplexer_1 (
    .in0(RA_Address_t), .in1(adder_2_out), .out(multiplexer_1_out), .sel(BranchMux));
  Bit_Extender #(.in_width(26), .out_width(24)) bit_extender_2 (.in(Inst_Address), .out(bit_extender_2_out));
  Bit_Extender #(.in_width(32), .out_width(24)) bit_extender_3 (.in(RG_Address), .out(bit_extender_3_out));
  Multiplexer #(.width(24), .disabled(0), .enable("false")) multiplexer_2 (
    .in0(bit_extender_2_out), .in1(bit_extender_3_out), .out(multiplexer_2_out), .sel(JumpReg));
  Multiplexer #(.width(24), .disabled(0), .enable("false")) multiplexer_3 (
    .in0(multiplexer_1_out), .in1(multiplexer_2_out), .out(multiplexer_3_out), .sel(Jump));
  Register #(.width(24)) PC (.D(multiplexer_3_out), .Q(PC_Address), .clk(Clock), .clr(Reset));  // open: en
  assign RA_Address = {{8{RA_Address_t[23]}}, RA_Address_t};  // Bit_Extender bit_extender_4

  // Other names for the same wires on the sheet: CLK = Clock; Imm[15:0] = Immediate
endmodule

module Imm_ZeroExt (
  input  [15:0] Imm,
  input  ZeroExt,
  output [31:0] Imm32b
);

  wire [31:0] bit_extender_1_out, bit_extender_2_out;

  assign bit_extender_1_out = {{16{Imm[15]}}, Imm};  // Bit_Extender bit_extender_1
  assign bit_extender_2_out = {{16{1'b0}}, Imm};  // Bit_Extender bit_extender_2
  Multiplexer #(.width(32), .disabled(0), .enable("false")) multiplexer_1 (
    .in0(bit_extender_1_out), .in1(bit_extender_2_out), .out(Imm32b), .sel(ZeroExt));
endmodule

module Extend_Byte (
  input  [31:0] Mem_Data,
  input  Load_ZeroExt,
  input  AccessByte,
  output [31:0] MemData_Out
);

  wire [7:0] bit_extender_1_out;
  wire [31:0] bit_extender_2_out, bit_extender_3_out, multiplexer_1_out;

  Bit_Extender #(.in_width(32), .out_width(8)) bit_extender_1 (.in(Mem_Data), .out(bit_extender_1_out));
  assign bit_extender_2_out = {{24{bit_extender_1_out[7]}}, bit_extender_1_out};  // Bit_Extender bit_extender_2
  Multiplexer #(.width(32), .disabled(0), .enable("false")) multiplexer_1 (
    .in0(bit_extender_2_out), .in1(bit_extender_3_out), .out(multiplexer_1_out), .sel(Load_ZeroExt));
  assign bit_extender_3_out = {{24{1'b0}}, bit_extender_1_out};  // Bit_Extender bit_extender_3
  Multiplexer #(.width(32), .disabled(0), .enable("false")) multiplexer_2 (
    .in0(Mem_Data), .in1(multiplexer_1_out), .out(MemData_Out), .sel(AccessByte));
endmodule

module NOP (
  input  JUMP,
  input  Branch,
  input  BranchEQ,
  input  Equal,
  output NOP
);

  wire and_1_out, xnor_1_out;

  and and_1 (and_1_out, Branch, xnor_1_out);
  xnor xnor_1 (xnor_1_out, BranchEQ, Equal);
  or or_1 (NOP, JUMP, and_1_out);
endmodule
