// Logisim project mem.circ as structural Verilog: 3 circuits, main circuit main
module main (
  input  [31:0] Data_Mem_Addr,
  input  [31:0] Data_Mem_In,
  input  ACCESS_BYTE,
  input  MEM_WRITE,
  input  CLOCK,
  output [31:0] Data_Mem_Out
);

  wire not_1_out;
  wire [1:0] Byte_Address;
  wire [23:0] Wd_Address;
  wire [31:0] RAM_DataOut;

  _32b_byte_to_24b_wd_address u_32b_byte_to_24b_wd_address_1 (
    ._32b_Byte_Address(Data_Mem_Addr), .Last_2_Bytes(Byte_Address), ._24b_Address(Wd_Address));
  RAM_wd_or_byte_select ram_wd_or_byte_select_1 (
    .RAM_DataOut(RAM_DataOut), .Byte_Address(Byte_Address), .Byte(ACCESS_BYTE), .MEM_DataOut(Data_Mem_Out));
  assign RAM_DataOut = MEM_WRITE ? Data_Mem_In : 32'bz;  // Controlled_Buffer controlled_buffer_1
  not not_1 (not_1_out, MEM_WRITE);
  RAM #(.addrWidth(24), .dataWidth(32)) ram_1 (
    .addr(Wd_Address), .data(RAM_DataOut), .sel(1'b1), .clk(CLOCK), .ld(not_1_out), .clr(1'b0));

  // Other names for the same wires on the sheet: Byte = ACCESS_BYTE; CLK = CLOCK; DataIn[31:0] = Data_Mem_In;
  //   MEM_DataOut[31:0] = Data_Mem_Out; MemWrite = MEM_WRITE

  // Notes on the sheet:
  //   These are INPUTS to the circuit
  //   These are INPUTS to the circuit
  //   DO NOT CHANGE THE LOCATIONS OF THE INPUTS/OUTPUTS! IF YOU DO SO, YOU NEED TO MAKE SURE THE PINS ARE AT THE RIGHT PLACE!
  //   Yet again, the clock is not an actual clock, but an input, one that will be driven from a higher circuit
  //   This is an OUTPUT to the circuit
endmodule

module _32b_byte_to_24b_wd_address (
  input  [31:0] _32b_Byte_Address,
  output [1:0] Last_2_Bytes,
  output [23:0] _24b_Address
);


  assign _24b_Address = _32b_Byte_Address[25:2];
  assign Last_2_Bytes = _32b_Byte_Address[1:0];
endmodule

module RAM_wd_or_byte_select (
  input  [31:0] RAM_DataOut,
  input  [1:0] Byte_Address,
  input  Byte,
  output [31:0] MEM_DataOut
);

  wire [7:0] multiplexer_1_out;
  wire [31:0] bit_extender_1_out;

  Multiplexer #(.select(2), .width(8), .disabled(0), .enable("false")) multiplexer_1 (
    .in0(RAM_DataOut[7:0]), .in1(RAM_DataOut[15:8]), .in2(RAM_DataOut[23:16]), .in3(RAM_DataOut[31:24]),
    .out(multiplexer_1_out), .sel(Byte_Address));
  assign bit_extender_1_out = {{24{1'b0}}, multiplexer_1_out};  // Bit_Extender bit_extender_1
  Multiplexer #(.width(32), .disabled(0), .enable("false")) multiplexer_2 (
    .in0(RAM_DataOut), .in1(bit_extender_1_out), .out(MEM_DataOut), .sel(Byte));
endmodule
