// Logisim project regfile.circ as structural Verilog: 1 circuit, main circuit main
module main (
  input  [1:0] Read_register_1,
  input  [1:0] Read_register_2,
  input  [1:0] write_register,
  input  [31:0] write_data,
  input  RegWrite,
  input  clock,
  output [31:0] t0_Value,
  output [31:0] t1_Value,
  output [31:0] t2_Value,
  output [31:0] t3_Value,
  output [31:0] Read_Data_1,
  output [31:0] Read_Data_2
);

  wire Write_T0, Write_T1, Write_T2, Write_T3;

  Register #(.width(32)) T0_Reg (.D(write_data), .en(Write_T0), .Q(t0_Value), .clk(clock));  // open: clr
  Register #(.width(32)) T1_Reg (.D(write_data), .en(Write_T1), .Q(t1_Value), .clk(clock));  // open: clr
  Register #(.width(32)) T2_Reg (.D(write_data), .en(Write_T2), .Q(t2_Value), .clk(clock));  // open: clr
  Register #(.width(32)) T3_Reg (.D(write_data), .en(Write_T3), .Q(t3_Value), .clk(clock));  // open: clr
  Demultiplexer #(.select(2), .disabled(0), .enable("false")) demultiplexer_1 (
    .out0(Write_T0), .out1(Write_T1), .out2(Write_T2), .out3(Write_T3), .in(RegWrite), .sel(write_register));
  Multiplexer #(.select(2), .width(32), .disabled(0), .enable("false")) multiplexer_1 (
    .in0(t0_Value), .in1(t1_Value), .in2(t2_Value), .in3(t3_Value), .out(Read_Data_1), .sel(Read_register_1));
  Multiplexer #(.select(2), .width(32), .disabled(0), .enable("false")) multiplexer_2 (
    .in0(t0_Value), .in1(t1_Value), .in2(t2_Value), .in3(t3_Value), .out(Read_Data_2), .sel(Read_register_2));

  // Other names for the same wires on the sheet: Clk = clock; Reg1R[1:0] = Read_register_1;
  //   Reg2R[1:0] = Read_register_2; T0[31:0] = t0_Value; T1[31:0] = t1_Value; T2[31:0] = t2_Value;
  //   T3[31:0] = t3_Value; WriteData[31:0] = write_data; WriteReg_prime[1:0] = write_register

  // Notes on the sheet:
  //   These are INPUTS to the circuit
  //   These are INPUTS to the circuit
  //   DO NOT CHANGE THE LOCATIONS OF THE INPUTS/OUTPUTS! IF YOU DO SO, YOU NEED TO MAKE SURE THE PINS ARE AT THE RIGHT PLACE!
  //   These are OUTPUTS to the circuit
  //   Yet again, the clock is not an actual clock, but an input, one that will be driven from a higher circuit
  //   These are OUTPUTS to the circuit
endmodule
