// Logisim project Lab 6.circ as structural Verilog
module Ex1 (
  input  [7:0] Input,
  output [7:0] Out1,
  output [7:0] Out2,
  output [7:0] out_4
);

  wire and_2_out, not_9_out;
  wire [7:0] adder_1_out, not_1_out, undriven, undriven_2;

  not not_1 (not_1_out[0], Input[0]);
  not not_2 (not_1_out[1], Input[1]);
  not not_3 (not_1_out[2], Input[2]);
  not not_4 (not_1_out[3], Input[3]);
  not not_5 (not_1_out[4], Input[4]);
  not not_6 (not_1_out[5], Input[5]);
  not not_7 (not_1_out[6], Input[6]);
  not not_8 (not_1_out[7], Input[7]);
  assign Out1 = undriven & undriven_2;  // AND_Gate and_1, 8 bits wide
  Adder adder_1 (.a(not_1_out), .b(8'h1f), .out(adder_1_out));  // open: cin, cout
  and and_2 (and_2_out, not_1_out[0], not_1_out[1], not_1_out[2], not_1_out[3], not_1_out[5], not_1_out[6], not_1_out[4], Input[7]);
  not not_9 (not_9_out, and_2_out);
  assign out_4 = {{7{not_9_out}}, not_9_out};  // Bit_Extender bit_extender_1
  assign Out2 = adder_1_out & out_4;  // AND_Gate and_3, 8 bits wide
endmodule

module Rotota_Subplexer (
  input  [15:0] in_1,
  input  [3:0] in_2,
  input  [3:0] in_3,
  output out_4
);

  wire [3:0] adder_1_out;

  Multiplexer #(.select(4)) multiplexer_1 (
    .in0(in_1[0]), .in1(in_1[1]), .in2(in_1[2]), .in3(in_1[3]), .in4(in_1[4]), .in5(in_1[5]), .in6(in_1[6]),
    .in7(in_1[7]), .in8(in_1[8]), .in9(in_1[9]), .in10(in_1[10]), .in11(in_1[11]), .in12(in_1[12]),
    .in13(in_1[13]), .in14(in_1[14]), .in15(in_1[15]), .out(out_4), .sel(adder_1_out));  // open: en
  Adder #(.width(4)) adder_1 (.a(in_2), .b(in_3), .out(adder_1_out));  // open: cin, cout
endmodule

module Rotate (
  input  [15:0] in_1,
  input  [3:0] in_2,
  output [15:0] out_3
);

  Rotota_Subplexer rotota_subplexer_1 (.in_1(in_1), .in_2(in_2), .in_3(4'b0000), .out_4(out_3[0]));
  Rotota_Subplexer rotota_subplexer_2 (.in_1(in_1), .in_2(in_2), .in_3(4'b0001), .out_4(out_3[1]));
  Rotota_Subplexer rotota_subplexer_3 (.in_1(in_1), .in_2(in_2), .in_3(4'b0010), .out_4(out_3[2]));
  Rotota_Subplexer rotota_subplexer_4 (.in_1(in_1), .in_2(in_2), .in_3(4'b0011), .out_4(out_3[3]));
  Rotota_Subplexer rotota_subplexer_5 (.in_1(in_1), .in_2(in_2), .in_3(4'b0100), .out_4(out_3[4]));
  Rotota_Subplexer rotota_subplexer_6 (.in_1(in_1), .in_2(in_2), .in_3(4'b0101), .out_4(out_3[5]));
  Rotota_Subplexer rotota_subplexer_7 (.in_1(in_1), .in_2(in_2), .in_3(4'b0110), .out_4(out_3[6]));
  Rotota_Subplexer rotota_subplexer_8 (.in_1(in_1), .in_2(in_2), .in_3(4'b0111), .out_4(out_3[7]));
  Rotota_Subplexer rotota_subplexer_9 (.in_1(in_1), .in_2(in_2), .in_3(4'b1000), .out_4(out_3[8]));
  Rotota_Subplexer rotota_subplexer_10 (.in_1(in_1), .in_2(in_2), .in_3(4'b1001), .out_4(out_3[9]));
  Rotota_Subplexer rotota_subplexer_11 (.in_1(in_1), .in_2(in_2), .in_3(4'b1010), .out_4(out_3[10]));
  Rotota_Subplexer rotota_subplexer_12 (.in_1(in_1), .in_2(in_2), .in_3(4'b1011), .out_4(out_3[11]));
  Rotota_Subplexer rotota_subplexer_13 (.in_1(in_1), .in_2(in_2), .in_3(4'b1100), .out_4(out_3[12]));
  Rotota_Subplexer rotota_subplexer_14 (.in_1(in_1), .in_2(in_2), .in_3(4'b1101), .out_4(out_3[13]));
  Rotota_Subplexer rotota_subplexer_15 (.in_1(in_1), .in_2(in_2), .in_3(4'b1110), .out_4(out_3[14]));
  Rotota_Subplexer rotota_subplexer_16 (.in_1(in_1), .in_2(in_2), .in_3(4'b1111), .out_4(out_3[15]));
endmodule
